# Fritzing sketch Ultra Sonic Sensor (saved by Fritzing 0.9.3b)

parts:
  hc-sr1 = hc-sr04
  Part1 = Arduino Uno (Rev3)

nets:
  VCC: hc-sr1.VCC, Part1.5V
  N1: hc-sr1.Trig, Part1.D7
  N2: hc-sr1.Echo, Part1.D6_PWM
  GND: hc-sr1.GND, Part1.GND
