# Fritzing sketch Control_LED_with_Bluetooth (saved by Fritzing 0.9.3b)

parts:
  LED1 = LED - 5mm [color="Red (633nm)" package="5 mm [THT]"]
  R1 = Resistor [tolerance=±5% resistance=220 package=THT]
  Part1 = Arduino Uno (Rev3)
  Part2 = Bluetooth HC-05 Macho

nets:
  GND: LED1.cathode, Part1.GND, Part2.GND
  N1: LED1.anode, R1.Pin_0
  N2: R1.Pin_1, Part1.D13/SCK
  N3: Part1.D0/RX, Part2.TXD
  N4: Part1.D1/TX, Part2.RXD
  5V: Part1.5V, Part2.VCC
