# Fritzing sketch Microphone Sensor (saved by Fritzing 0.9.3b)

parts:
  Part1 = Arduino Uno (Rev3)
  Part2 = KY-037 High Sensitivity Sound Detection Module [package="Breakout board"]

nets:
  N1: Part1.D8, Part2.D0
  N2: Part1.GND, Part2.G
  N3: Part1.5V, Part2.+

custom parts:
  KY-037 High Sensitivity Sound Detection Module: KY-037 high sensitivity sound detection module is an analog/digital sensor that uses a condenser microphone to observe changes in environment noise.
