# Fritzing sketch PIR_SENSOR (saved by Fritzing 0.9.3b)

parts:
  Part1 = Arduino Uno (Rev3)
  PIR2 = PIR sensor

nets:
  N1: Part1.D13/SCK, PIR2.SIG
  5V: Part1.5V, PIR2.VDD
  GND: Part1.GND, PIR2.GND
