# Fritzing sketch IR_sensor_code (saved by Fritzing 0.9.3b)

parts:
  Part1 = Arduino Uno (Rev3)
  M1 = fc-51 [package=THT]

nets:
  N1: Part1.D10_PWM/SS, M1.pin1
  N2: Part1.5V, M1.pin3
  N3: Part1.GND, M1.pin2
