# Fritzing sketch Soil Moisture Sensor (saved by Fritzing 0.9.3b)

parts:
  Part1 = Arduino Uno (Rev3)
  Part2 = Soil Moisture Sensor

nets:
  GND: Part1.GND, Part2.GND
  N1: Part1.D6_PWM, Part2.SIG
  5V: Part1.5V, Part2.VCC
